// Logisim project ALU.circ as structural Verilog: 1 circuit, main circuit main
module main (
  input  [7:0] A,
  input  [7:0] B,
  input  [3:0] Instruction,
  output [7:0] Output,
  output LZ,
  output EQ,
  output GZ,
  output LE,
  output GE
);

  wire [7:0] adder_1_out, multiplier_1_out, subtractor_1_out;

  Comparator comparator_1 (.a(A), .b({8{1'b0}}), .gt(GZ), .eq(EQ), .lt(LZ));
  or or_1 (LE, LZ, EQ);
  Adder adder_1 (.a(A), .b(B), .out(adder_1_out));  // open: cin, cout
  Subtractor subtractor_1 (.a(A), .b(B), .out(subtractor_1_out));  // open: bin, bout
  Multiplier multiplier_1 (.a(A), .b(B), .out(multiplier_1_out));  // open: cin, cout
  or or_2 (GE, EQ, GZ);
  Multiplexer #(.select(4), .width(8), .enable("false")) multiplexer_1 (
    .in0({8{1'b0}}), .in1({8{1'b0}}), .in2({8{1'b0}}), .in3({8{1'b0}}), .in4(adder_1_out),
    .in5(subtractor_1_out), .in6({8{1'b0}}), .in7(multiplier_1_out), .in8({8{1'b0}}), .in9({8{1'b0}}),
    .in10({8{1'b0}}), .in11({8{1'b0}}), .in12({8{1'b0}}), .in13({8{1'b0}}), .in14({8{1'b0}}),
    .in15({8{1'b0}}), .out(Output), .sel(Instruction));
endmodule
