// Logisim project final.circ as structural Verilog: 3 circuits, main circuit main
// %ecx
module main (
  input  [31:0] in_1,
  input  [15:0] in_2,
  input  in_3,
  input  in_4,
  input  [2:0] in_5,
  input  [31:0] in_6,
  input  [2:0] in_7,
  input  in_8,
  input  in_9,
  input  [2:0] in_10,
  input  [2:0] in_11,
  input  [31:0] in_12,
  output [31:0] out_13,
  output [31:0] out_14,
  output [31:0] out_15
);

  wire clock_1_out, clock_2_out;

  Clock clock_1 (.out(clock_1_out));
  memory_bus memory_bus_1 (.Address(in_2), .WE(in_3), .RE(in_4), .Write_Data(in_1), .Read_Data(out_13));
  Clock clock_2 (.out(clock_2_out));
  _8x32_RF u_8x32_rf_1 (
    .Write1(in_6), .Register_1_2(in_7), .WE(in_9), .Register_2_2(in_10), .Write2(in_12), .Read1(out_14),
    .RE(in_8), .Register_1(in_5), .Read2(out_15), .Register_2(in_11));
endmodule

module _8x32_RF (
  input  [31:0] Write1,
  input  RE,
  input  [2:0] Register_1,
  input  [2:0] Register_1_2,
  input  WE,
  input  [2:0] Register_2,
  input  [2:0] Register_2_2,
  input  [31:0] Write2,
  output [31:0] Read1,
  output [31:0] Read2
);

  wire clock_1_out, decoder_1_out0, decoder_1_out1, decoder_1_out2, decoder_1_out3, decoder_1_out4,
       decoder_1_out5, decoder_1_out6, decoder_1_out7, decoder_2_out0, decoder_2_out1, decoder_2_out2,
       decoder_2_out3, decoder_2_out4, decoder_2_out5, decoder_2_out6, decoder_2_out7, decoder_3_out0,
       decoder_3_out1, decoder_3_out2, decoder_3_out3, decoder_3_out4, decoder_3_out5, decoder_3_out6,
       decoder_3_out7, decoder_4_out0, decoder_4_out1, decoder_4_out2, decoder_4_out3, decoder_4_out4,
       decoder_4_out5, decoder_4_out6, decoder_4_out7, or_1_out, or_2_out, or_3_out, or_4_out, or_5_out,
       or_6_out, or_7_out, or_8_out;
  wire [31:0] eax_q, ebp_q, ebx_q, ecx_q, edi_q, edx_q, esi_q, esp_q, multiplexer_1_out, multiplexer_2_out,
       multiplexer_3_out, multiplexer_4_out, multiplexer_5_out, multiplexer_6_out, multiplexer_7_out,
       multiplexer_8_out;

  Decoder #(.select(3)) decoder_1 (
    .out0(decoder_1_out0), .out1(decoder_1_out1), .out2(decoder_1_out2), .out3(decoder_1_out3),
    .out4(decoder_1_out4), .out5(decoder_1_out5), .out6(decoder_1_out6), .out7(decoder_1_out7),
    .sel(Register_1_2), .en(WE));
  Decoder #(.select(3)) decoder_2 (
    .out0(decoder_2_out0), .out1(decoder_2_out1), .out2(decoder_2_out2), .out3(decoder_2_out3),
    .out4(decoder_2_out4), .out5(decoder_2_out5), .out6(decoder_2_out6), .out7(decoder_2_out7),
    .sel(Register_2_2), .en(WE));
  Multiplexer #(.width(32)) multiplexer_1 (
    .in0(Write2), .in1(Write1), .out(multiplexer_1_out), .sel(decoder_1_out0));  // open: en
  Multiplexer #(.width(32)) multiplexer_2 (
    .in0(Write2), .in1(Write1), .out(multiplexer_2_out), .sel(decoder_1_out1));  // open: en
  Multiplexer #(.width(32)) multiplexer_3 (
    .in0(Write2), .in1(Write1), .out(multiplexer_3_out), .sel(decoder_1_out2));  // open: en
  Multiplexer #(.width(32)) multiplexer_4 (
    .in0(Write2), .in1(Write1), .out(multiplexer_4_out), .sel(decoder_1_out3));  // open: en
  Multiplexer #(.width(32)) multiplexer_5 (
    .in0(Write2), .in1(Write1), .out(multiplexer_5_out), .sel(decoder_1_out4));  // open: en
  Multiplexer #(.width(32)) multiplexer_6 (
    .in0(Write2), .in1(Write1), .out(multiplexer_6_out), .sel(decoder_1_out5));  // open: en
  Multiplexer #(.width(32)) multiplexer_7 (
    .in0(Write2), .in1(Write1), .out(multiplexer_7_out), .sel(decoder_1_out6));  // open: en
  Multiplexer #(.width(32)) multiplexer_8 (
    .in0(Write2), .in1(Write1), .out(multiplexer_8_out), .sel(decoder_1_out7));  // open: en
  or or_1 (or_1_out, decoder_1_out0, decoder_2_out0);
  or or_2 (or_2_out, decoder_1_out1, decoder_2_out1);
  or or_3 (or_3_out, decoder_1_out2, decoder_2_out2);
  or or_4 (or_4_out, decoder_1_out3, decoder_2_out3);
  or or_5 (or_5_out, decoder_1_out4, decoder_2_out4);
  or or_6 (or_6_out, decoder_1_out5, decoder_2_out5);
  or or_7 (or_7_out, decoder_1_out6, decoder_2_out6);
  or or_8 (or_8_out, decoder_1_out7, decoder_2_out7);
  Clock clock_1 (.out(clock_1_out));
  Register #(.width(32)) eax (.D(multiplexer_1_out), .en(or_1_out), .Q(eax_q), .clk(clock_1_out));  // open: clr
  Register #(.width(32)) ecx (.D(multiplexer_2_out), .en(or_2_out), .Q(ecx_q), .clk(clock_1_out));  // open: clr
  Register #(.width(32)) edx (.D(multiplexer_3_out), .en(or_3_out), .Q(edx_q), .clk(clock_1_out));  // open: clr
  Register #(.width(32)) ebx (.D(multiplexer_4_out), .en(or_4_out), .Q(ebx_q), .clk(clock_1_out));  // open: clr
  Register #(.width(32)) esi (.D(multiplexer_5_out), .en(or_5_out), .Q(esi_q), .clk(clock_1_out));  // open: clr
  Register #(.width(32)) edi (.D(multiplexer_6_out), .en(or_6_out), .Q(edi_q), .clk(clock_1_out));  // open: clr
  Register #(.width(32)) esp (.D(multiplexer_7_out), .en(or_7_out), .Q(esp_q), .clk(clock_1_out));  // open: clr
  Register #(.width(32)) ebp (.D(multiplexer_8_out), .en(or_8_out), .Q(ebp_q), .clk(clock_1_out));  // open: clr
  assign Read1 = decoder_3_out0 ? eax_q : 32'bz;  // Controlled_Buffer controlled_buffer_1
  assign Read1 = decoder_3_out1 ? ecx_q : 32'bz;  // Controlled_Buffer controlled_buffer_2
  assign Read1 = decoder_3_out2 ? edx_q : 32'bz;  // Controlled_Buffer controlled_buffer_3
  assign Read1 = decoder_3_out3 ? ebx_q : 32'bz;  // Controlled_Buffer controlled_buffer_4
  assign Read1 = decoder_3_out4 ? esi_q : 32'bz;  // Controlled_Buffer controlled_buffer_5
  assign Read1 = decoder_3_out5 ? edi_q : 32'bz;  // Controlled_Buffer controlled_buffer_6
  assign Read1 = decoder_3_out6 ? esp_q : 32'bz;  // Controlled_Buffer controlled_buffer_7
  assign Read1 = decoder_3_out7 ? ebp_q : 32'bz;  // Controlled_Buffer controlled_buffer_8
  assign Read2 = decoder_4_out0 ? eax_q : 32'bz;  // Controlled_Buffer controlled_buffer_9
  assign Read2 = decoder_4_out1 ? ecx_q : 32'bz;  // Controlled_Buffer controlled_buffer_10
  assign Read2 = decoder_4_out2 ? edx_q : 32'bz;  // Controlled_Buffer controlled_buffer_11
  assign Read2 = decoder_4_out3 ? ebx_q : 32'bz;  // Controlled_Buffer controlled_buffer_12
  assign Read2 = decoder_4_out4 ? esi_q : 32'bz;  // Controlled_Buffer controlled_buffer_13
  assign Read2 = decoder_4_out5 ? edi_q : 32'bz;  // Controlled_Buffer controlled_buffer_14
  assign Read2 = decoder_4_out6 ? esp_q : 32'bz;  // Controlled_Buffer controlled_buffer_15
  assign Read2 = decoder_4_out7 ? ebp_q : 32'bz;  // Controlled_Buffer controlled_buffer_16
  Decoder #(.select(3)) decoder_3 (
    .out0(decoder_3_out0), .out1(decoder_3_out1), .out2(decoder_3_out2), .out3(decoder_3_out3),
    .out4(decoder_3_out4), .out5(decoder_3_out5), .out6(decoder_3_out6), .out7(decoder_3_out7),
    .sel(Register_1), .en(RE));
  Decoder #(.select(3)) decoder_4 (
    .out0(decoder_4_out0), .out1(decoder_4_out1), .out2(decoder_4_out2), .out3(decoder_4_out3),
    .out4(decoder_4_out4), .out5(decoder_4_out5), .out6(decoder_4_out6), .out7(decoder_4_out7),
    .sel(Register_2), .en(RE));
endmodule

module memory_bus (
  input  [15:0] Address,
  input  [31:0] Write_Data,
  input  WE,
  input  RE,
  output [31:0] Read_Data
);

  wire clock_1_out, not_1_out;
  wire [31:0] ram_1_data;

  Clock clock_1 (.out(clock_1_out));
  RAM #(.addrWidth(16), .dataWidth(32)) ram_1 (
    .addr(Address), .data(ram_1_data), .clk(clock_1_out), .ld(not_1_out));  // open: sel, clr
  not not_1 (not_1_out, WE);
  assign ram_1_data = WE ? Read_Data : 32'bz;  // Controlled_Buffer controlled_buffer_1
  assign Read_Data = RE ? ram_1_data : 32'bz;  // Controlled_Buffer controlled_buffer_2
  assign Read_Data = WE ? Write_Data : 32'bz;  // Controlled_Buffer controlled_buffer_3
endmodule
